# Fritzing sketch FritzingSchema (saved by Fritzing 0.9.3b)
breadboards: 3

parts:
  Raspberry_Pi_1 = Raspberry Pi 3 [part_number=RPI-3-V1.2]
  Componente1 = Arduino Leonardo (Rev3b)
  YwRobot_Power_Supply1 = YwRobot Breadboard Power Supply [part_number=545043]
  T1 = LM35 Temperature Sensor [package="TO92 [THT]"]
  LED1 = LEDs [package=led10mm]
  LED2 = LEDs [package=led10mm]
  LED3 = LEDs [package=led10mm]
  R1 = Resistor [tolerance=±1% resistance=220 package=THT]
  R2 = Resistor [tolerance=±1% resistance=220 package=THT]
  R3 = Resistor [tolerance=±1% resistance=220 package=THT]
  R4 = Resistor [tolerance=±1% resistance=220 package=THT]
  R5 = Resistor [tolerance=±1% resistance=220 package=THT]
  LED5 = LEDs [package=led10mm]
  LED4 = LEDs [package=led10mm]
  S1 = Pushbutton [package="[SMD]"]
  S2 = Pushbutton [package="[SMD]"]
  S3 = Pushbutton [package="[SMD]"]
  S4 = Pushbutton [package="[SMD]"]
  D1 = LTE-302 [package=lte-302]
  D2 = LTE-302 [package=lte-302]
  D3 = LTE-302 [package=lte-302]
  D4 = LTE-302 [package=lte-302]
  LED6 = Infrared LED - 5mm [package="5 mm [THT]"]
  LED7 = Infrared LED - 5mm [package="5 mm [THT]"]
  LED8 = Infrared LED - 5mm [package="5 mm [THT]"]
  LED9 = Infrared LED - 5mm [package="5 mm [THT]"]
  R6 = Resistor [tolerance=±5% resistance=100 package=THT]
  R7 = Resistor [tolerance=±5% resistance=100 package=THT]
  R8 = Resistor [tolerance=±5% resistance=100 package=THT]
  R9 = Resistor [tolerance=±5% resistance=100 package=THT]
  R10 = Resistor [tolerance=±5% resistance=10k package="0402 [SMD]"]
  R11 = Resistor [tolerance=±5% resistance=10k package="0402 [SMD]"]
  R12 = Resistor [tolerance=±5% resistance=10k package="0402 [SMD]"]
  R13 = Resistor [tolerance=±5% resistance=10k package="0402 [SMD]"]

nets:
  3V3: Raspberry_Pi_1.3v3, Raspberry_Pi_1.3V3, S1.Pin_3, S1.Pin_4, S2.Pin_4, S3.Pin_3, S3.Pin_4, S4.Pin_3, S4.Pin_4
  N1: Raspberry_Pi_1.GPIO2, R5.Pin_0
  N2: Raspberry_Pi_1.GPIO3, R1.Pin_0
  N3: Raspberry_Pi_1.GIPO4, R2.Pin_0
  N4: Raspberry_Pi_1.GIPO17, R3.Pin_0
  N5: Raspberry_Pi_1.GIPO27, R4.Pin_0
  N6: Raspberry_Pi_1.GIPO6, LED9.cathode, R13.Pin_0
  N7: Raspberry_Pi_1.GIPO13, LED8.cathode, R12.Pin_0
  N8: Raspberry_Pi_1.GIPO19, LED7.cathode, R11.Pin_0
  N9: Raspberry_Pi_1.GIPO26, LED6.cathode, R10.Pin_0
  N10: Raspberry_Pi_1.GIPO21, S1.Pin_2
  N11: Raspberry_Pi_1.GIPO20, S2.Pin_2
  N12: Raspberry_Pi_1.GIPO16, S3.Pin_1, S3.Pin_2
  N13: Raspberry_Pi_1.GND, LED1.C, LED2.C, LED3.C, LED5.C, LED4.C
  N14: Raspberry_Pi_1.GIPO12, S4.Pin_1, S4.Pin_2
  N15: Componente1.5V, T1.+Vs
  GND: Componente1.GND, T1.GND
  N16: Componente1.A0, T1.Vout
  N17: YwRobot_Power_Supply1.VCC#5, YwRobot_Power_Supply1.VCC#6
  N18: YwRobot_Power_Supply1.VCC#9, YwRobot_Power_Supply1.VCC#10, R6.Pin_0, R7.Pin_0, R8.Pin_0, R9.Pin_0, R10.Pin_1, R11.Pin_1, R12.Pin_1, R13.Pin_1
  N19: YwRobot_Power_Supply1.GND, D1.C, D2.C, D3.C, D4.C, LED6.anode, LED7.anode, LED8.anode, LED9.anode
  N20: LED1.A, R3.Pin_1
  N21: LED2.A, R4.Pin_1
  N22: LED3.A, R5.Pin_1
  N23: R1.Pin_1, LED5.A
  N24: R2.Pin_1, LED4.A
  N25: D1.A, R6.Pin_1
  N26: D2.A, R7.Pin_1
  N27: D3.A, R8.Pin_1
  N28: D4.A, R9.Pin_1

custom parts:
  YwRobot Breadboard Power Supply: The YwRobot Breadboard Power Supply (MB-V2) has two power rails; they can be 5V or 3V3. Power to the module can be provided through the female USB socket or through the A10 (female) 2.1mm power jack.
  Infrared LED - 5mm: A generic infrared LED (~1.2V)
